# Fritzing sketch StratoballOON (saved by Fritzing 0.9.3b)
breadboards: 1

parts:
  MASTER = Arduino Pro Mini v13
  BAT1 = Battery Holders [package=battery-aa-panel]
  IC1 = Voltage Regulator [package=78xxl]
  Composant8 = BME280 Breakout
  MicroSD = OpenLog
  GY-NEO6MV3 = SUP500F [package=sup500f]
  R2 = Resistor [tolerance=±5% resistance=4.7k package="0402 [SMD]"]
  R3 = Resistor [tolerance=±5% resistance=10k package="0402 [SMD]"]
  R4 = Resistor [tolerance=±5% resistance=1k package="0402 [SMD]"]
  LED2 = LEDs [package=led10mm]
  Composant9 = Real Time Clock Module - DS1307 RTC Breakout Board
  S3 = Pushbutton [package="[SMD]"]
  S4 = Pushbutton [package="[SMD]"]
  DS1 = DS18B20 1-Wire Temperature Sensor [part_number=DS18B20]
  R5 = Resistor [tolerance=±5% resistance=4.7k package="2512 [SMD]"]
  Composant10 = Adafruit Si7021 Temp Humidity [part_number="Adafruit #3251"]

nets:
  VCC: MASTER.VCC, Composant8.3.3V, MicroSD.VCC, R4.Pin_1, S4.Pin_1, S4.Pin_2, Composant10.+3V3
  GND: MASTER.GND, BAT1.-, IC1.GND, Composant8.GND, MicroSD.GND, GY-NEO6MV3.GND, R3.Pin_1, Composant9.GND, DS1.GND, Composant10.GND
  N1: MASTER.A4, Composant8.SDI/SDA, Composant9.SDA, Composant10.SDA
  N2: MASTER.A5, Composant8.SCK/SCL, Composant9.SCL, Composant10.SCL
  N3: MASTER.RAW, GY-NEO6MV3.VCC
  N4: MASTER.D13/SCK, MicroSD.SCK
  N5: MASTER.D12/MISO, MicroSD.MOSI
  N6: MASTER.D11_PWM/MOSI, MicroSD.MISO
  N7: MASTER.D10_PWM/SS, DS1.DQ, R5.Pin_1
  N8: MASTER.D9_PWM, S4.Pin_3, S4.Pin_4
  N9: MASTER.D8, MicroSD.RST
  N10: MASTER.D4, GY-NEO6MV3.TX-O
  N11: MASTER.D3_PWM, R2.Pin_1, R3.Pin_0
  N12: BAT1.+, S3.Pin_3, S3.Pin_4
  N13: IC1.IN, S3.Pin_1, S3.Pin_2
  5V: IC1.OUT, Composant9.5V, DS1.VDD, R5.Pin_0
  N14: GY-NEO6MV3.RX-I, R2.Pin_0
  N15: R4.Pin_0, LED2.A

notes:
  GND: Black
  VCC: Red
  RX: Yellow
  TX: Green

custom parts:
  Adafruit Si7021 Temp Humidity: It's summer and you're sweating and your hair's all frizzy and all you really want to know is why the weatherman said this morning that today's relative humidity would max out at a perfectly reasonable 42% when it feels more like 77%. Enter the Si7021 Temperature + Humidity Sensor - the best way to prove the weatherman wrong! This lovely sensor for Silicon labs has ± 3% relative humidity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
